# Fritzing sketch 3_sonar (saved by Fritzing 0.8.7b)
breadboards: 1

parts:
  Part1 = Arduino Yun
  Part2 = SRF05 Ultrasonic Rangefinder

nets:
  N1: Part1.D11_PWM/MOSI, Part2.Echo
  N2: Part1.D12/MISO, Part2.Trig
  5V: Part1.5V, Part2.VCC
  GND: Part1.GND, Part2.GND

custom parts:
  Arduino Yun: The new Arduino Yun is a microcontroller board based on the ATmega32u4 (datasheet) and the Atheros AR9331. The Atheros processor supports a Linux distribution based on OpenWRT named Linino. The board has built-in Ethernet and WiFi support, a USB-A port, micro-SD card slot, 20 digital input/output pins (of which 7 can be used as PWM outputs and 12 as analog inputs), a 16 MHz crystal oscillator,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
