# Fritzing sketch 4_meteo_bh (saved by Fritzing 0.8.7b)
breadboards: 1

parts:
  Part3 = suda
  Part4 = Arduino Uno (Rev3)

nets:
  N1: Part3.SDA, Part4.A4/SDA
  N2: Part3.SCL, Part4.A5/SCL
  GND: Part3.GND, Part4.GND
  VCC: Part3.VCC, Part4.5V
