# Fritzing sketch 4_meteo_dht (saved by Fritzing 0.8.7b)
breadboards: 1

parts:
  Part1 = Arduino Yun
  DHT1 = DHT11 Humitidy and Temperature Sensor

nets:
  N1: Part1.D7, DHT1.DATA
  5V: Part1.5V, DHT1.VDD
  GND: Part1.GND, DHT1.GND

custom parts:
  Arduino Yun: The new Arduino Yun is a microcontroller board based on the ATmega32u4 (datasheet) and the Atheros AR9331. The Atheros processor supports a Linux distribution based on OpenWRT named Linino. The board has built-in Ethernet and WiFi support, a USB-A port, micro-SD card slot, 20 digital input/output pins (of which 7 can be used as PWM outputs and 12 as analog inputs), a 16 MHz crystal oscillator,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
  DHT11 Humitidy and Temperature Sensor: DHT11 Humidity and Temperature Sensor
