# Fritzing sketch 4_meteo_vcnl (saved by Fritzing 0.8.7b)
breadboards: 1

parts:
  Part4 = Arduino Uno (Rev3)
  SENSOR1 = VCNL4000

nets:
  N1: Part4.A4/SDA, SENSOR1.SDA
  N2: Part4.A5/SCL, SENSOR1.SCL
  5V: Part4.5V, SENSOR1.3.3V
  GND: Part4.GND, SENSOR1.GND

custom parts:
  VCNL4000: TCS34725 RGB Color Sensor with LED
