# Fritzing sketch complete (saved by Fritzing 0.8.7b)
breadboards: 1

parts:
  DHT1 = DHT11 Humitidy and Temperature Sensor
  PIR1 = PIR sensor
  Part2 = SRF05 Ultrasonic Rangefinder
  Part4 = Arduino Uno (Rev3)
  SENSOR1 = VCNL4000

nets:
  VDD: DHT1.VDD, PIR1.VDD, Part2.VCC, Part4.5V, SENSOR1.3.3V
  N1: DHT1.DATA, Part4.D7
  GND: DHT1.GND, PIR1.GND, Part2.GND, Part4.GND, SENSOR1.GND
  N2: PIR1.SIG, Part4.D5_PWM
  N3: Part2.Trig, Part4.D12/MISO
  N4: Part2.Echo, Part4.D11_PWM/MOSI
  N5: Part4.A4/SDA, SENSOR1.SDA
  N6: Part4.A5/SCL, SENSOR1.SCL

custom parts:
  DHT11 Humitidy and Temperature Sensor: DHT11 Humidity and Temperature Sensor
  VCNL4000: TCS34725 RGB Color Sensor with LED
